// Logisim project 7SegmentDisplay.circ as structural Verilog: 1 circuit, main circuit main
module main (
  input  [3:0] number,
  output A,
  output B,
  output C,
  output D,
  output E,
  output F,
  output DG
);

  wire and_1_out, and_2_out, and_3_out, and_4_out, and_5_out, and_6_out, and_7_out, and_8_out, and_9_out,
       and_10_out, and_11_out, and_12_out, and_13_out, and_14_out, and_15_out, and_16_out, and_17_out,
       and_18_out, and_19_out, and_20_out, and_21_out, and_22_out, and_23_out, and_24_out, and_25_out,
       and_26_out, and_27_out;

  and and_1 (and_1_out, ~number[3], number[1]);  // AND_Gate
  and and_2 (and_2_out, ~number[3], number[2], number[0]);  // AND_Gate
  and and_3 (and_3_out, ~number[2], ~number[1], ~number[0]);  // AND_Gate
  and and_4 (and_4_out, number[3], ~number[2], ~number[1]);  // AND_Gate
  and and_5 (and_5_out, ~number[3], ~number[1], ~number[0]);  // AND_Gate
  and and_6 (and_6_out, ~number[2], ~number[1], ~number[0]);  // AND_Gate
  and and_7 (and_7_out, ~number[3], number[1], number[0]);  // AND_Gate
  and and_8 (and_8_out, ~number[3], ~number[2], number[1]);  // AND_Gate
  and and_9 (and_9_out, number[3], ~number[2], ~number[1]);  // AND_Gate
  and and_10 (and_10_out, ~number[3], number[2]);  // AND_Gate
  and and_11 (and_11_out, ~number[3], ~number[1], ~number[0]);  // AND_Gate
  and and_12 (and_12_out, ~number[3], number[1], number[0]);  // AND_Gate
  and and_13 (and_13_out, number[3], ~number[2], ~number[1]);  // AND_Gate
  and and_14 (and_14_out, ~number[3], number[2], ~number[1], number[0]);  // AND_Gate
  and and_15 (and_15_out, ~number[2], ~number[1], ~number[0]);  // AND_Gate
  and and_16 (and_16_out, ~number[3], ~number[2], number[1]);  // AND_Gate
  and and_17 (and_17_out, ~number[3], number[1], ~number[0]);  // AND_Gate
  and and_18 (and_18_out, ~number[2], ~number[1], ~number[0]);  // AND_Gate
  and and_19 (and_19_out, ~number[3], ~number[2], ~number[1]);  // AND_Gate
  and and_20 (and_20_out, ~number[3], number[1], ~number[0]);  // AND_Gate
  and and_21 (and_21_out, ~number[3], ~number[1]);  // AND_Gate
  and and_22 (and_22_out, number[3], ~number[2], ~number[1]);  // AND_Gate
  and and_23 (and_23_out, ~number[3], number[2], ~number[0], number[1]);  // AND_Gate
  and and_24 (and_24_out, number[3], ~number[2], ~number[1]);  // AND_Gate
  and and_25 (and_25_out, ~number[3], number[2], ~number[1]);  // AND_Gate
  and and_26 (and_26_out, ~number[3], ~number[2], number[1]);  // AND_Gate
  and and_27 (and_27_out, ~number[3], number[1], ~number[0]);  // AND_Gate
  or or_1 (A, and_1_out, and_2_out, and_3_out, and_4_out);
  or or_2 (B, and_5_out, and_6_out, and_7_out, and_8_out, and_9_out);
  or or_3 (C, and_10_out, and_11_out, and_12_out, and_13_out);
  or or_4 (D, and_14_out, and_15_out, and_16_out, and_17_out);
  or or_5 (E, and_18_out, and_19_out, and_20_out);
  or or_6 (F, and_21_out, and_22_out, and_23_out);
  or or_7 (DG, and_24_out, and_25_out, and_26_out, and_27_out);
endmodule
