// Logisim project Scoreboard.circ as structural Verilog: 1 circuit, main circuit main
module main (
  input  Human,
  input  Machina,
  output [3:0] HumanResult,
  output [3:0] MachinaResult
);

  Counter #(.width(4), .max('hf)) counter_1 (
    .D(4'b0000), .Q(HumanResult), .clk(Human));  // open: load, count, carry, clr
  Counter #(.width(4), .max('hf)) counter_2 (
    .D(4'b0000), .Q(MachinaResult), .clk(Machina));  // open: load, count, carry, clr
endmodule
