// Logisim project datapath3.circ as structural Verilog: 1 circuit, main circuit main
module main (
  input  clock,
  input  [7:0] came,
  input  endgame1,
  input  resetregister,
  input  endgame2,
  input  [7:0] _1,
  input  s0,
  input  [7:0] _2,
  input  s2,
  input  s1,
  input  endgame3,
  input  [7:0] _3,
  input  [7:0] _4,
  input  [7:0] _5,
  input  [7:0] _6,
  input  [7:0] _7,
  input  [7:0] _8,
  input  endgame8,
  input  endgame5,
  input  endgame7,
  input  endgame6,
  input  endgame4,
  input  letter,
  input  resetwrong,
  output [3:0] letter_number,
  output Win,
  output [7:0] letter_2,
  output \continue ,
  output [3:0] wrong
);

  wire and_1_out, and_2_out, comparator_1_eq, comparator_1_gt, comparator_1_lt, comparator_2_eq,
       comparator_2_gt, comparator_2_lt, comparator_3_eq, comparator_3_gt, comparator_3_lt, comparator_4_eq,
       comparator_4_gt, comparator_4_lt, comparator_5_eq, comparator_5_gt, comparator_5_lt, comparator_6_eq,
       comparator_6_gt, comparator_6_lt, comparator_7_eq, comparator_7_gt, comparator_7_lt, comparator_8_eq,
       comparator_8_gt, comparator_8_lt, comparator_9_eq, comparator_10_eq, comparator_11_eq,
       comparator_12_eq, comparator_13_eq, comparator_13_gt, comparator_14_eq, comparator_15_eq,
       comparator_16_eq, comparator_17_eq, comparator_18_eq, comparator_18_lt, multiplexer_1_out,
       multiplexer_2_out, multiplexer_3_out, multiplexer_4_out, multiplexer_5_out, multiplexer_6_out,
       multiplexer_10_out, multiplexer_17_out, not_1_out, not_2_out, not_3_out, not_4_out, not_5_out,
       not_6_out, not_7_out, not_8_out, or_1_out, or_2_out, or_3_out, or_4_out, or_5_out, or_6_out, or_7_out,
       or_8_out, or_9_out, register_2_q, register_3_q, register_4_q, register_5_q, register_6_q,
       register_7_q, register_8_q, register_9_q;
  wire [3:0] bitadder_2_out;
  wire [7:0] multiplexer_7_out, multiplexer_8_out, multiplexer_9_out, multiplexer_11_out, multiplexer_12_out,
       multiplexer_13_out, multiplexer_14_out, multiplexer_16_out, register_1_q;

  Register register_1 (.D(came), .en(letter), .Q(register_1_q), .clk(clock));  // open: clr
  Comparator #(.mode("unsigned")) comparator_1 (
    .a(_1), .b(register_1_q), .gt(comparator_1_gt), .eq(comparator_1_eq), .lt(comparator_1_lt));
  Comparator #(.mode("unsigned")) comparator_2 (
    .a(_2), .b(register_1_q), .gt(comparator_2_gt), .eq(comparator_2_eq), .lt(comparator_2_lt));
  Comparator #(.mode("unsigned")) comparator_3 (
    .a(_3), .b(register_1_q), .gt(comparator_3_gt), .eq(comparator_3_eq), .lt(comparator_3_lt));
  Comparator #(.mode("unsigned")) comparator_4 (
    .a(_4), .b(register_1_q), .gt(comparator_4_gt), .eq(comparator_4_eq), .lt(comparator_4_lt));
  Comparator #(.mode("unsigned")) comparator_5 (
    .a(_5), .b(register_1_q), .gt(comparator_5_gt), .eq(comparator_5_eq), .lt(comparator_5_lt));
  Comparator #(.mode("unsigned")) comparator_6 (
    .a(_6), .b(register_1_q), .gt(comparator_6_gt), .eq(comparator_6_eq), .lt(comparator_6_lt));
  Comparator #(.mode("unsigned")) comparator_7 (
    .a(_7), .b(register_1_q), .gt(comparator_7_gt), .eq(comparator_7_eq), .lt(comparator_7_lt));
  Comparator #(.mode("unsigned")) comparator_8 (
    .a(_8), .b(register_1_q), .gt(comparator_8_gt), .eq(comparator_8_eq), .lt(comparator_8_lt));
  or or_1 (or_1_out, comparator_1_gt, comparator_1_lt);
  LED Eq1 (.in(comparator_1_eq));
  LED Eq2 (.in(comparator_2_eq));
  or or_2 (or_2_out, comparator_2_gt, comparator_2_lt);
  LED Eq3 (.in(comparator_3_eq));
  or or_3 (or_3_out, comparator_3_gt, comparator_3_lt);
  LED Eq4 (.in(comparator_4_eq));
  or or_4 (or_4_out, comparator_4_gt, comparator_4_lt);
  LED LessorBigT4 (.in(or_4_out));
  LED Eq5 (.in(comparator_5_eq));
  or or_5 (or_5_out, comparator_5_gt, comparator_5_lt);
  LED Eq6 (.in(comparator_6_eq));
  or or_6 (or_6_out, comparator_6_gt, comparator_6_lt);
  LED Eq7 (.in(comparator_7_eq));
  LED LessorBigT7 (.in(or_7_out));
  or or_7 (or_7_out, comparator_7_gt, comparator_7_lt);
  LED Eq8 (.in(comparator_8_eq));
  or or_8 (or_8_out, comparator_8_gt, comparator_8_lt);
  LED LessorBigT1 (.in(or_1_out));
  LED LessorBigT2 (.in(or_2_out));
  LED LessorBigT3 (.in(or_3_out));
  LED LessorBigT5 (.in(or_5_out));
  LED LessorBigT6 (.in(or_6_out));
  LED LessorBigT8 (.in(or_8_out));
  Multiplexer #(.enable("false")) multiplexer_1 (
    .in0(comparator_1_eq), .in1(1'b1), .out(multiplexer_1_out), .sel(endgame1));
  Multiplexer #(.enable("false")) multiplexer_2 (
    .in0(comparator_3_eq), .in1(1'b1), .out(multiplexer_2_out), .sel(endgame3));
  Multiplexer #(.enable("false")) multiplexer_3 (
    .in0(comparator_5_eq), .in1(1'b1), .out(multiplexer_3_out), .sel(endgame5));
  and and_1 (and_1_out, or_1_out, or_2_out, or_3_out, or_4_out, or_6_out, or_7_out, or_5_out, or_8_out);
  Multiplexer #(.enable("false")) multiplexer_4 (
    .in0(comparator_2_eq), .in1(1'b1), .out(multiplexer_4_out), .sel(endgame2));
  Multiplexer #(.enable("false")) multiplexer_5 (
    .in0(comparator_4_eq), .in1(1'b1), .out(multiplexer_5_out), .sel(endgame4));
  Register #(.width(1)) register_2 (
    .D(comparator_5_eq), .en(multiplexer_3_out), .Q(register_2_q), .clk(clock), .clr(resetregister));
  Multiplexer #(.enable("false")) multiplexer_6 (
    .in0(comparator_6_eq), .in1(1'b1), .out(multiplexer_6_out), .sel(endgame6));
  and and_2 (and_2_out, and_1_out, letter);
  Register #(.width(1)) register_3 (
    .D(comparator_1_eq), .en(multiplexer_1_out), .Q(register_3_q), .clk(clock), .clr(resetregister));
  Register #(.width(1)) register_4 (
    .D(comparator_2_eq), .en(multiplexer_4_out), .Q(register_4_q), .clk(clock), .clr(resetregister));
  Register #(.width(1)) register_5 (
    .D(comparator_3_eq), .en(multiplexer_2_out), .Q(register_5_q), .clk(clock), .clr(resetregister));
  Register #(.width(1)) register_6 (
    .D(comparator_4_eq), .en(multiplexer_5_out), .Q(register_6_q), .clk(clock), .clr(resetregister));
  Register #(.width(1)) register_7 (
    .D(comparator_6_eq), .en(multiplexer_6_out), .Q(register_7_q), .clk(clock), .clr(resetregister));
  Counter #(.width(4), .max('hf)) counter_1 (
    .D(4'b0000), .Q(wrong), .clk(and_2_out), .clr(resetwrong));  // open: load, count, carry
  Multiplexer #(.width(8), .enable("false")) multiplexer_7 (
    .in0(8'h23), .in1(_1), .out(multiplexer_7_out), .sel(register_3_q));
  Multiplexer #(.width(8), .enable("false")) multiplexer_8 (
    .in0(8'h23), .in1(_3), .out(multiplexer_8_out), .sel(register_5_q));
  Multiplexer #(.width(8), .enable("false")) multiplexer_9 (
    .in0(8'h23), .in1(_6), .out(multiplexer_9_out), .sel(register_7_q));
  Multiplexer #(.enable("false")) multiplexer_10 (
    .in0(comparator_7_eq), .in1(1'b1), .out(multiplexer_10_out), .sel(endgame7));
  Comparator #(.mode("unsigned")) comparator_9 (.a(_3), .b({8{1'b0}}), .eq(comparator_9_eq));  // open: gt, lt
  Comparator #(.mode("unsigned")) comparator_10 (.a(_4), .b({8{1'b0}}), .eq(comparator_10_eq));  // open: gt, lt
  Comparator #(.mode("unsigned")) comparator_11 (.a(_5), .b({8{1'b0}}), .eq(comparator_11_eq));  // open: gt, lt
  Comparator #(.mode("unsigned")) comparator_12 (.a(_7), .b({8{1'b0}}), .eq(comparator_12_eq));  // open: gt, lt
  Multiplexer #(.width(8), .enable("false")) multiplexer_11 (
    .in0(8'h23), .in1(_2), .out(multiplexer_11_out), .sel(register_4_q));
  Multiplexer #(.width(8), .enable("false")) multiplexer_12 (
    .in0(8'h23), .in1(_4), .out(multiplexer_12_out), .sel(register_6_q));
  Multiplexer #(.width(8), .enable("false")) multiplexer_13 (
    .in0(8'h23), .in1(_5), .out(multiplexer_13_out), .sel(register_2_q));
  Register #(.width(1)) register_8 (
    .D(comparator_7_eq), .en(multiplexer_10_out), .Q(register_8_q), .clk(clock), .clr(resetregister));
  Comparator #(.width(4), .mode("unsigned")) comparator_13 (
    .a(wrong), .b(4'b1010), .gt(comparator_13_gt), .eq(comparator_13_eq), .lt(\continue ));
  Comparator #(.mode("unsigned")) comparator_14 (.a(_1), .b({8{1'b0}}), .eq(comparator_14_eq));  // open: gt, lt
  Comparator #(.mode("unsigned")) comparator_15 (.a(_2), .b({8{1'b0}}), .eq(comparator_15_eq));  // open: gt, lt
  Comparator #(.mode("unsigned")) comparator_16 (.a(_6), .b({8{1'b0}}), .eq(comparator_16_eq));  // open: gt, lt
  Comparator #(.mode("unsigned")) comparator_17 (.a(_8), .b({8{1'b0}}), .eq(comparator_17_eq));  // open: gt, lt
  not not_1 (not_1_out, comparator_14_eq);
  not not_2 (not_2_out, comparator_15_eq);
  not not_3 (not_3_out, comparator_9_eq);
  not not_4 (not_4_out, comparator_10_eq);
  not not_5 (not_5_out, comparator_11_eq);
  not not_6 (not_6_out, comparator_16_eq);
  not not_7 (not_7_out, comparator_12_eq);
  not not_8 (not_8_out, comparator_17_eq);
  Multiplexer #(.width(8), .enable("false")) multiplexer_14 (
    .in0(8'h23), .in1(_7), .out(multiplexer_14_out), .sel(register_8_q));
  or or_9 (or_9_out, comparator_13_gt, comparator_13_eq);
  BitAdder #(.width(1)) bitadder_1 (
    .in0(not_1_out), .in1(not_2_out), .in2(not_3_out), .in3(not_4_out), .in4(not_5_out), .in5(not_6_out),
    .in6(not_7_out), .in7(not_8_out), .out(letter_number));
  Multiplexer #(.select(3), .width(8), .enable("false")) multiplexer_15 (
    .in0(multiplexer_7_out), .in1(multiplexer_11_out), .in2(multiplexer_8_out), .in3(multiplexer_12_out),
    .in4(multiplexer_13_out), .in5(multiplexer_9_out), .in6(multiplexer_14_out), .in7(multiplexer_16_out),
    .out(letter_2), .sel({s2, s1, s0}));
  Multiplexer #(.width(8), .enable("false")) multiplexer_16 (
    .in0(8'h23), .in1(_8), .out(multiplexer_16_out), .sel(register_9_q));
  Multiplexer #(.enable("false")) multiplexer_17 (
    .in0(comparator_8_eq), .in1(1'b1), .out(multiplexer_17_out), .sel(endgame8));
  LED end_game (.in(or_9_out));
  BitAdder #(.width(1)) bitadder_2 (
    .in0(register_4_q), .in1(register_6_q), .in2(register_5_q), .in3(register_2_q), .in4(register_7_q),
    .in5(register_8_q), .in6(register_9_q), .in7(register_3_q), .out(bitadder_2_out));
  Register #(.width(1)) register_9 (
    .D(comparator_8_eq), .en(multiplexer_17_out), .Q(register_9_q), .clk(clock), .clr(resetregister));
  Comparator #(.width(4), .mode("unsigned")) comparator_18 (
    .a(letter_number), .b(bitadder_2_out), .eq(comparator_18_eq), .lt(comparator_18_lt));  // open: gt
  or or_10 (Win, comparator_18_eq, comparator_18_lt);
  // OR_Gate or_11 is placed but not wired
endmodule
