// Logisim project led_matrix.circ as structural Verilog: 1 circuit, main circuit main
module main (
  input  [3:0] hanging,
  output [31:0] First4,
  output [31:0] LastFour
);

  Multiplexer #(.select(4), .width(32), .enable("false")) multiplexer_1 (
    .in0({32{1'b0}}), .in1(32'h1010101), .in2(32'h1010101), .in3(32'h81818101), .in4(32'h81e18101),
    .in5(32'ha1e1a121), .in6(32'ha1f1a121), .in7(32'ha1f9a121), .in8(32'ha9f9a121), .in9(32'ha9f9a921),
    .in10(32'ha9fda921), .in11({32{1'b0}}), .in12({32{1'b0}}), .in13({32{1'b0}}), .in14({32{1'b0}}),
    .in15({32{1'b0}}), .out(LastFour), .sel(hanging));
  Multiplexer #(.select(4), .width(32), .enable("false")) multiplexer_2 (
    .in0({32{1'b0}}), .in1(32'h1010101), .in2(32'h1ff0101), .in3(32'h1ff8181), .in4(32'h1ff8181),
    .in5(32'h1ff81a1), .in6(32'h1ff81a1), .in7(32'h1ff81a1), .in8(32'h1ff81a1), .in9(32'h1ff81a1),
    .in10(32'h1ff81a1), .in11({32{1'b0}}), .in12({32{1'b0}}), .in13({32{1'b0}}), .in14({32{1'b0}}),
    .in15({32{1'b0}}), .out(First4), .sel(hanging));
  DotMatrix #(.matrixcols(8), .matrixrows(8)) dotmatrix_1 (
    .col0(First4[31:24]), .col1(First4[23:16]), .col2(First4[15:8]), .col3(First4[7:0]),
    .col4(LastFour[31:24]), .col5(LastFour[23:16]), .col6(LastFour[15:8]), .col7(LastFour[7:0]));
endmodule
