// Logisim project lettercircuit.circ as structural Verilog: 1 circuit, main circuit main
module main (
  input  A,
  input  B,
  input  C,
  input  D,
  input  E,
  input  F,
  input  G,
  input  H,
  input  I,
  input  J,
  input  K,
  input  L,
  input  M,
  input  N,
  input  O,
  input  P,
  input  Q,
  input  R,
  input  S,
  input  T,
  input  U,
  input  V,
  input  W,
  input  X,
  input  Y,
  input  Z,
  output [7:0] letter,
  output pushed
);

  or or_1 (pushed, A, B, C, D, E, F, G, H, I, J, K, L, M, O, N, P, Q, R, S, T, U, V, W, X, Y, Z);
  or or_2 (letter[4], T, P, Q, R, S, U, V, X, Y, Z);
  or or_3 (letter[2], D, E, F, G, L, M, N, O, T, U, V, W);
  or or_4 (letter[3], H, I, J, K, L, M, N, O, X, Y, Z);
  or or_5 (letter[1], B, C, F, G, J, K, N, O, R, S, V, W, Z);
  or or_6 (letter[0], A, C, E, G, I, K, M, O, Q, S, U, W, Y);

  assign letter[7:5] = 3'b011;
endmodule
