// Logisim project main.circ as structural Verilog: 1 circuit, main circuit main
module main (
  input  [7:0] in_1,
  input  [7:0] in_2,
  input  [7:0] in_3,
  input  [7:0] in_4,
  input  [7:0] in_5,
  input  [7:0] in_6,
  input  [7:0] in_7,
  input  [7:0] in_8
);

  wire a_out, b_out, c_out, clock_1_out, d_out, e_out, f_out, g_out, h_out, i_out, j_out, k_out, l_out,
       m_out, main_1_enable, main_1_endgames, main_1_resetregister, main_1_resetwrong, main_1_s0, main_1_s1,
       main_1_s2, main_1_ttyclear, main_2_a, main_2_b, main_2_c, main_2_d, main_2_dg, main_2_e, main_2_f,
       main_3_continue, main_3_win, main_4_pushed, main_7_a, main_7_b, main_7_c, main_7_d, main_7_dg,
       main_7_e, main_7_f, main_8_a, main_8_c, main_8_d, main_8_dg, main_8_e, main_8_f, n_out, not_1_out,
       o_out, p_out, q_out, r_out, Reset_out, s_out, t_out, u_out, v_out, w_out, x_out, y_out, z_out;
  wire [3:0] main_3_letter_number, main_3_wrong, main_6_humanresult, main_6_machinaresult;
  wire [6:0] bit_extender_1_out;
  wire [7:0] letter_q, main_3_letter_2, main_4_letter;
  wire [31:0] main_5_first4, main_5_lastfour;

  Button Reset (.out(Reset_out));
  controlunit6_main main_1 (
    .reset(Reset_out), .letter(main_4_pushed), .\continue (main_3_continue), .win(main_3_win),
    .clock(clock_1_out), .resetwrong(main_1_resetwrong), .ttyclear(main_1_ttyclear),
    .endgames(main_1_endgames), .resetregister(main_1_resetregister), .S2(main_1_s2), .S1(main_1_s1),
    .S0(main_1_s0), .enable(main_1_enable));
  Button a (.out(a_out));
  Button d (.out(d_out));
  Button c (.out(c_out));
  Button b (.out(b_out));
  Button e (.out(e_out));
  Button f (.out(f_out));
  Button g (.out(g_out));
  Button h (.out(h_out));
  _7SegmentDisplay_main main_2 (
    .number(main_3_letter_number), .A(main_2_a), .B(main_2_b), .C(main_2_c), .D(main_2_d), .E(main_2_e),
    .F(main_2_f), .DG(main_2_dg));
  _7_Segment_Display u_7_segment_display_1 (
    .g(main_2_dg), .f(main_2_f), .a(main_2_a), .b(main_2_b), .e(main_2_e), .d(main_2_d), .c(main_2_c));  // open: dp
  Clock clock_1 (.out(clock_1_out));
  datapath3_main main_3 (
    .clock(clock_1_out), .came(letter_q), .resetregister(main_1_resetregister), ._1(in_1), .s0(main_1_s0),
    ._2(in_2), .s2(main_1_s2), .endgame3(main_1_endgames), ._3(in_3), ._4(in_4), ._5(in_5), ._6(in_6),
    ._7(in_7), ._8(in_8), .letter(main_4_pushed), .resetwrong(main_1_resetwrong),
    .letter_number(main_3_letter_number), .Win(main_3_win), .endgame1(main_1_endgames),
    .endgame2(main_1_endgames), .letter_2(main_3_letter_2), .s1(main_1_s1), .endgame8(main_1_endgames),
    .endgame5(main_1_endgames), .endgame7(main_1_endgames), .endgame6(main_1_endgames),
    .endgame4(main_1_endgames), .\continue (main_3_continue), .wrong(main_3_wrong));
  Button i (.out(i_out));
  lettercircuit_main main_4 (
    .A(a_out), .B(b_out), .C(c_out), .D(d_out), .E(e_out), .F(f_out), .G(g_out), .H(h_out), .I(i_out),
    .J(j_out), .K(k_out), .L(l_out), .M(m_out), .N(n_out), .O(o_out), .P(p_out), .Q(q_out), .R(r_out),
    .S(s_out), .T(t_out), .U(u_out), .V(v_out), .W(w_out), .X(x_out), .Y(y_out), .Z(z_out),
    .letter(main_4_letter), .pushed(main_4_pushed));
  Button k (.out(k_out));
  Button j (.out(j_out));
  Register letter (.D(main_4_letter), .en(main_4_pushed), .Q(letter_q), .clk(clock_1_out));  // open: clr
  Button m (.out(m_out));
  Button l (.out(l_out));
  Button n (.out(n_out));
  Button o (.out(o_out));
  Button p (.out(p_out));
  led_matrix_main main_5 (.First4(main_5_first4), .hanging(main_3_wrong), .LastFour(main_5_lastfour));
  Button r (.out(r_out));
  Button q (.out(q_out));
  Button s (.out(s_out));
  Button t (.out(t_out));
  Button u (.out(u_out));
  Button w (.out(w_out));
  Button v (.out(v_out));
  DotMatrix #(.matrixcols(8), .matrixrows(8)) dotmatrix_1 (
    .col0(main_5_first4[31:24]), .col1(main_5_first4[23:16]), .col2(main_5_first4[15:8]),
    .col3(main_5_first4[7:0]), .col4(main_5_lastfour[31:24]), .col5(main_5_lastfour[23:16]),
    .col6(main_5_lastfour[15:8]), .col7(main_5_lastfour[7:0]));
  Button y (.out(y_out));
  Button x (.out(x_out));
  Button z (.out(z_out));
  Bit_Extender #(.out_width(7)) bit_extender_1 (.in(main_3_letter_2), .out(bit_extender_1_out));
  TTY tty_1 (.data(bit_extender_1_out), .clk(clock_1_out), .we(main_1_enable), .clr(main_1_ttyclear));
  not not_1 (not_1_out, main_3_continue);
  Scoreboard_main main_6 (
    .Human(main_3_win), .Machina(not_1_out), .HumanResult(main_6_humanresult),
    .MachinaResult(main_6_machinaresult));
  _7_Segment_Display u_7_segment_display_2 (
    .g(main_7_dg), .f(main_7_f), .a(main_7_a), .b(main_7_b), .e(main_7_e), .d(main_7_d), .c(main_7_c));  // open: dp
  _7SegmentDisplay_main main_7 (
    .number(main_6_humanresult), .A(main_7_a), .B(main_7_b), .C(main_7_c), .D(main_7_d), .E(main_7_e),
    .F(main_7_f), .DG(main_7_dg));
  _7SegmentDisplay_main main_8 (
    .number(main_6_machinaresult), .A(main_8_a), .B(main_8_a), .C(main_8_c), .D(main_8_d), .E(main_8_e),
    .F(main_8_f), .DG(main_8_dg));
  _7_Segment_Display u_7_segment_display_3 (
    .g(main_8_dg), .f(main_8_f), .a(main_8_a), .b(main_8_a), .e(main_8_e), .d(main_8_d), .c(main_8_c));  // open: dp

  // Notes on the sheet:
  //   Control Unit
  //   DataPath
  //   Human
  //   Machina
endmodule
