// Logisim project controlunit.circ as structural Verilog: 1 circuit, main circuit main
module main (
  input  Go,
  input  Lt,
  input  Eq,
  input  Gt,
  input  Clk,
  output LA,
  output LB,
  output Mult,
  output S_A_B,
  output S__1_m,
  output sub_add,
  output SA,
  output Res
);

  wire and_2_out, and_3_out, and_4_out, not_1_out, not_2_out, not_3_out, not_4_out, not_5_out, not_6_out,
       not_7_out, not_8_out, not_9_out, not_10_out, not_11_out, not_12_out, not_13_out, or_1_out, or_3_out,
       xor_1_out;
  wire [2:0] and_5_out, register_1_q;

  or or_1 (or_1_out, Lt, Eq);
  Register #(.width(3)) register_1 (.D(and_5_out), .en(1'b1), .Q(register_1_q), .clk(Clk));  // open: clr
  not not_1 (not_1_out, register_1_q[2]);
  and and_1 (and_5_out[2], or_1_out, not_1_out, register_1_q[1], register_1_q[0]);
  xor xor_1 (xor_1_out, register_1_q[0], register_1_q[1]);
  not not_2 (not_2_out, register_1_q[2]);
  and and_2 (and_2_out, Gt, not_2_out, register_1_q[1], register_1_q[0]);
  and and_3 (and_3_out, xor_1_out, not_3_out);
  not not_3 (not_3_out, register_1_q[2]);
  or or_2 (and_5_out[1], and_2_out, and_3_out);
  and S1 (LB, register_1_q[0], not_4_out, not_5_out);
  not not_4 (not_4_out, register_1_q[1]);
  not not_5 (not_5_out, register_1_q[2]);
  not not_6 (not_6_out, register_1_q[0]);
  and S2 (S__1_m, not_6_out, register_1_q[1], not_7_out);
  not not_7 (not_7_out, register_1_q[2]);
  and S3 (SA, register_1_q[0], register_1_q[1], not_8_out);
  not not_8 (not_8_out, register_1_q[2]);
  not not_9 (not_9_out, register_1_q[1]);
  not not_10 (not_10_out, register_1_q[0]);
  and S4 (Res, not_9_out, not_10_out, register_1_q[2]);
  and and_4 (and_4_out, Go, not_11_out);
  not not_11 (not_11_out, register_1_q[1]);
  or or_3 (or_3_out, and_4_out, register_1_q[1]);
  not not_12 (not_12_out, register_1_q[2]);
  and and_5 (and_5_out[0], or_3_out, not_12_out, not_13_out);
  not not_13 (not_13_out, register_1_q[0]);
  or or_4 (Mult, LB, S__1_m, Res);
  or or_5 (LA, LB, SA);

  assign S_A_B = S__1_m;
  assign sub_add = S__1_m;
endmodule
