// Logisim project datapath.circ as structural Verilog: 1 circuit, main circuit main
module main (
  input  SA,
  input  [15:0] A,
  input  LA,
  input  S_A_B,
  input  Sub_Add,
  input  res,
  input  [15:0] B,
  input  Mult,
  input  LB,
  input  S_m__1,
  input  Clock,
  output Gt,
  output Eq,
  output Lt,
  output [15:0] result
);

  wire and_1_out, and_2_out, comparator_1_gt, comparator_1_lt, comparator_2_lt;
  wire [15:0] A_q, adder_1_out, B_q, demultiplexer_1_out0, demultiplexer_1_out1, Mult_q, multiplexer_1_out,
       multiplexer_2_out, multiplexer_3_out, multiplexer_4_out, multiplexer_5_out, multiplexer_6_out,
       multiplexer_7_out, negator_1_out, negator_2_out, negator_3_out;

  Comparator #(.width(16)) comparator_1 (
    .a(B), .b({16{1'b0}}), .gt(comparator_1_gt), .lt(comparator_1_lt));  // open: eq
  and and_1 (and_1_out, comparator_2_lt, comparator_1_lt);
  Comparator #(.width(16)) comparator_2 (.a(A), .b({16{1'b0}}), .lt(comparator_2_lt));  // open: gt, eq
  Negator #(.width(16)) negator_1 (.in(A), .out(negator_1_out));
  Multiplexer #(.width(16), .enable("false")) multiplexer_1 (
    .in0(A), .in1(negator_1_out), .out(multiplexer_1_out), .sel(and_1_out));
  and and_2 (and_2_out, comparator_2_lt, comparator_1_gt);
  Multiplexer #(.width(16), .enable("false")) multiplexer_2 (
    .in0(B), .in1(multiplexer_1_out), .out(multiplexer_2_out), .sel(and_2_out));
  Multiplexer #(.width(16), .enable("false")) multiplexer_3 (
    .in0(multiplexer_1_out), .in1(B), .out(multiplexer_3_out), .sel(and_2_out));
  Negator #(.width(16)) negator_2 (.in(multiplexer_2_out), .out(negator_2_out));
  Multiplexer #(.width(16), .enable("false")) multiplexer_4 (
    .in0(multiplexer_2_out), .in1(negator_2_out), .out(multiplexer_4_out), .sel(and_1_out));
  Multiplexer #(.width(16), .enable("false")) multiplexer_5 (
    .in0(multiplexer_3_out), .in1(demultiplexer_1_out0), .out(multiplexer_5_out), .sel(SA));
  Register #(.width(16)) u_B (.D(multiplexer_4_out), .en(LB), .Q(B_q), .clk(Clock));  // open: clr
  Register #(.width(16)) u_A (.D(multiplexer_5_out), .en(LA), .Q(A_q), .clk(Clock));  // open: clr
  Negator #(.width(16)) negator_3 (.in(16'h1), .out(negator_3_out));
  Comparator #(.width(16)) comparator_3 (.a(multiplexer_5_out), .b({16{1'b0}}), .gt(Gt), .eq(Eq), .lt(Lt));
  Multiplexer #(.width(16), .enable("false")) multiplexer_6 (
    .in0(A_q), .in1(B_q), .out(multiplexer_6_out), .sel(S_A_B));
  Multiplexer #(.width(16), .enable("false")) multiplexer_7 (
    .in0(negator_3_out), .in1(Mult_q), .out(multiplexer_7_out), .sel(S_m__1));
  Adder #(.width(16)) adder_1 (.a(multiplexer_6_out), .b(multiplexer_7_out), .out(adder_1_out));  // open: cin, cout
  Demultiplexer #(.width(16), .enable("false")) demultiplexer_1 (
    .out0(demultiplexer_1_out0), .out1(demultiplexer_1_out1), .in(adder_1_out), .sel(Sub_Add));
  Register #(.width(16)) u_Mult (.D(demultiplexer_1_out1), .en(Mult), .Q(Mult_q), .clk(Clock));  // open: clr
  Register #(.width(16)) u_result (.D(Mult_q), .en(res), .Q(result), .clk(Clock));  // open: clr
endmodule
