// Logisim project main.circ as structural Verilog: 1 circuit, main circuit main
module main (
  input  [15:0] B,
  input  [15:0] A,
  output [15:0] Result
);

  wire clock_1_out, main_1_la, main_1_lb, main_1_mult, main_1_res, main_1_s__1_m, main_1_s_a_b, main_1_sa,
       main_1_sub_add, main_2_eq, main_2_gt, main_2_lt, Start_out;

  Button Start (.out(Start_out));
  Clock clock_1 (.out(clock_1_out));
  controlunit_main main_1 (
    .Go(Start_out), .Lt(main_2_lt), .Eq(main_2_eq), .Gt(main_2_gt), .Clk(clock_1_out), .LA(main_1_la),
    .LB(main_1_lb), .Mult(main_1_mult), .S_A_B(main_1_s_a_b), .S__1_m(main_1_s__1_m),
    .sub_add(main_1_sub_add), .SA(main_1_sa), .Res(main_1_res));
  datapath_main main_2 (
    .SA(main_1_sa), .A(A), .LA(main_1_la), .S_A_B(main_1_s_a_b), .Sub_Add(main_1_sub_add), .res(main_1_res),
    .B(B), .Mult(main_1_mult), .LB(main_1_lb), .S_m__1(main_1_s__1_m), .Clock(clock_1_out), .Gt(main_2_gt),
    .Eq(main_2_eq), .Lt(main_2_lt), .result(Result));

  // Notes on the sheet:
  //   Firstly enter numbers in B and A then push the Start button to see result
endmodule
